# Fritzing sketch projekat - shema (saved by Fritzing 0.9.3b)

parts:
  SERVO1 = Tower Pro SG90 servo [part_number=101246]
  Keypad4x1 = Keypad Membran 4x4
  Mod2 = Raspberry Pi Pico W
  LCD3 = TFT 1.8 inch 160x128 w SD

nets:
  N1: SERVO1.Signal, Mod2.pin_34
  N2: SERVO1.+5V, Mod2.pin_40, LCD3.pin_1
  N3: SERVO1.GND, Mod2.pin_23, Mod2.pin_33, Mod2.pin_38, LCD3.pin2
  N4: Keypad4x1.Pin1, Mod2.pin_5
  N5: Keypad4x1.Pin2, Mod2.pin_4
  N6: Keypad4x1.Pin3, Mod2.pin_2
  N7: Keypad4x1.Pin4, Mod2.pin_1
  N8: Keypad4x1.Pin5, Mod2.pin_32
  N9: Keypad4x1.Pin6, Mod2.pin_31
  N10: Keypad4x1.Pin7, Mod2.pin_29
  N11: Keypad4x1.Pin8, Mod2.pin_27
  N12: Mod2.pin_14, LCD3.pin_7
  N13: Mod2.pin_15, LCD3.pin_6
  N14: Mod2.pin_21, LCD3.pin_5
  N15: Mod2.pin_22, LCD3.pin4
  N16: Mod2.pin_24, LCD3.pin3
  N17: Mod2.pin_36, LCD3.pin_8

custom parts:
  Tower Pro SG90 servo: Original file by John De Cristofaro http://www.adafruit.com/products/1449 Adafruit Feedback Servo (Small) Edited by: e-radionica.com 28/9/2015
  Keypad Membran 4x4: Membrane Keypad 4x4 Matrix
  Raspberry Pi Pico W: Raspberry Pi Pico W. Based around the RP2040 microcontroller the Pico W is a low cost microcontroller device bringing Raspberry Pi quality, cost, and easy of use to the microcontroller space. The areas marked KEEPOUT in pcb silkscreen should not have traces running through them to avoid shorts on a soldered in module!
  TFT 1.8 inch 160x128 w SD: This is a generic 1.8 tft spi lcd display available on ebay and others. The 1.8" display has 128x160 color pixels.
